# Fritzing sketch akıllı ev devre şeması  (saved by Fritzing 0.9.3b)
breadboards: 1

parts:
  Raspberry_Pi_1 = Raspberry Pi 3 [part_number=RPI-3-V1.2]
  J1 = Basic Servo
  J2 = Basic Servo
  IC1 = L293D [package=THT]
  M1 = DC Motor  # not connected
  M2 = DC Motor
  LED1 = smd LED [color="Red (633nm)" package="1206 [SMD]"]
  LED2 = smd LED [color="Red (633nm)" package="1206 [SMD]"]
  LED3 = smd LED [color="Red (633nm)" package="1206 [SMD]"]
  LED4 = smd LED [color="Red (633nm)" package="1206 [SMD]"]
  LED5 = smd LED [color="Red (633nm)" package="1206 [SMD]"]
  LED6 = smd LED [color="Red (633nm)" package="1206 [SMD]"]
  LED7 = smd LED [color="Red (633nm)" package="1206 [SMD]"]
  BAT1 = BC9VPC [package=bc9vpc]

nets:
  N1: Raspberry_Pi_1.GPIO17, J1.pulse
  N2: Raspberry_Pi_1.GPIO11, Raspberry_Pi_1.GPIO16, LED4.anode
  N3: Raspberry_Pi_1.GPIO13, LED2.anode
  N4: Raspberry_Pi_1.GPIO19, LED1.anode
  N5: Raspberry_Pi_1.GPIO26, LED6.anode
  N6: Raspberry_Pi_1.GPIO21, LED5.anode
  N7: Raspberry_Pi_1.GPIO20, LED7.anode
  N8: Raspberry_Pi_1.GPIO12, LED3.anode
  N9: Raspberry_Pi_1.GPIO25, IC1.Enable_1
  N10: Raspberry_Pi_1.GPIO24, IC1.In_1
  N11: Raspberry_Pi_1.GPIO23, IC1.In_2
  N12: Raspberry_Pi_1.GPIO18, J2.pulse
  GND: J1.gnd, J2.gnd, IC1.0V, LED1.cathode, LED2.cathode, LED4.cathode, LED5.cathode, LED6.cathode, LED7.cathode
  VCC: J1.vcc, J2.vcc
  N13: IC1.Out_1_(_Controlled_by_Enable_1_), M2.pin_2
  N14: IC1.Out_2_(_Controlled_by_Enable_1_), M2.pin_1
  N15: IC1.+Vmotor, BAT1.V+

notes:
  Evin Aydınlatma ışıkları
  Garaj-Dış Kapı motorları
  Isıtıcı-Klima motorları
  Motorların Yanındaki Ledler motorlrın çalışıp çalışmadığını kontrol etmek için konulmuştur!!!!
