# Fritzing sketch araç devre şeması (saved by Fritzing 0.9.3b)
breadboards: 1

parts:
  Raspberry_Pi_1 = Raspberry Pi 3 [part_number=RPI-3-V1.2]
  VCC1 = Battery block 9V
  M1 = DC Motor
  M2 = DC Motor
  S1 = H-Bridge with L298N
  S2 = H-Bridge with L298N
  M3 = DC Motor
  M4 = DC Motor

nets:
  N1: Raspberry_Pi_1.GIPO13, S1.IN2
  N2: Raspberry_Pi_1.GIPO19, S1.IN3
  N3: Raspberry_Pi_1.GIPO26, S1.IN4
  N4: Raspberry_Pi_1.GIPO12, S1.IN1
  GND: Raspberry_Pi_1.GND, S1.GND, S2.GND
  12V: VCC1.+, S1.12V, S2.12V
  N5: M1.pin_1, S1.M2-02
  N6: M1.pin_2, S1.M2-01
  N7: M2.pin_1, S1.M1-02
  N8: M2.pin_2, S1.M1-01
  N9: S2.M1-01, M4.pin_2
  N10: S2.M1-02, M4.pin_1
  N11: S2.M2-01, M3.pin_2
  N12: S2.M2-02, M3.pin_1

custom parts:
  H-Bridge with L298N: h-bridge
